# Fritzing sketch Potenciometro_leitor (saved by Fritzing 1.0.6)
breadboards: 1

parts:
  R1 = Rotary Potentiometer (Small) [maximum_resistance=10kΩ knob_status=50% power=0.5W package=THT]
  LED1 = smd LED [color="Red (633nm)" package="1206 [SMD]"]
  Componente1 = Arduino Uno (Rev3)

nets:
  N1: R1.leg1, Componente1.A0
  N2: R1.wiper, LED1.cathode, Componente1.GND
  N3: R1.leg2, Componente1.5V
  N4: LED1.anode, Componente1.D6_PWM
